// Logisim project microp.circ as structural Verilog: 7 circuits, main circuit RegisterFile
// Register File
module RegisterFile (
  input  [2:0] rd,
  input  [15:0] Datain,
  input  Register_Load,
  input  clock,
  output [15:0] Data_Out1,
  output [15:0] Data_Out2,
  output [15:0] Data_Out3,
  output [15:0] Data_Out4,
  output [15:0] Data_Out5,
  output [15:0] Data_Out6,
  output [15:0] Data_Out7,
  output [15:0] Data_Out8
);

  wire and_1_out, and_2_out, and_3_out, and_4_out, and_5_out, and_6_out, and_7_out, and_8_out,
       decoder_1_out0, decoder_1_out1, decoder_1_out2, decoder_1_out3, decoder_1_out4, decoder_1_out5,
       decoder_1_out6, decoder_1_out7;

  Decoder #(.select(3), .enable("false")) decoder_1 (
    .out0(decoder_1_out0), .out1(decoder_1_out1), .out2(decoder_1_out2), .out3(decoder_1_out3),
    .out4(decoder_1_out4), .out5(decoder_1_out5), .out6(decoder_1_out6), .out7(decoder_1_out7), .sel(rd));
  and and_1 (and_1_out, decoder_1_out0, Register_Load);
  and and_2 (and_2_out, decoder_1_out1, Register_Load);
  and and_3 (and_3_out, decoder_1_out2, Register_Load);
  and and_4 (and_4_out, decoder_1_out3, Register_Load);
  and and_5 (and_5_out, decoder_1_out4, Register_Load);
  and and_6 (and_6_out, decoder_1_out5, Register_Load);
  and and_7 (and_7_out, decoder_1_out6, Register_Load);
  and and_8 (and_8_out, decoder_1_out7, Register_Load);
  Register #(.width(16)) register_1 (.D(Datain), .en(and_1_out), .Q(Data_Out1), .clk(clock));  // open: clr
  Register #(.width(16)) register_2 (.D(Datain), .en(and_2_out), .Q(Data_Out2), .clk(clock));  // open: clr
  Register #(.width(16)) register_3 (.D(Datain), .en(and_3_out), .Q(Data_Out3), .clk(clock));  // open: clr
  Register #(.width(16)) register_4 (.D(Datain), .en(and_4_out), .Q(Data_Out4), .clk(clock));  // open: clr
  Register #(.width(16)) register_5 (.D(Datain), .en(and_5_out), .Q(Data_Out5), .clk(clock));  // open: clr
  Register #(.width(16)) register_6 (.D(Datain), .en(and_6_out), .Q(Data_Out6), .clk(clock));  // open: clr
  Register #(.width(16)) register_7 (.D(Datain), .en(and_7_out), .Q(Data_Out7), .clk(clock));  // open: clr
  Register #(.width(16)) register_8 (.D(Datain), .en(and_8_out), .Q(Data_Out8), .clk(clock));  // open: clr

  // Notes on the sheet:
  //   Register_Load: pull=down
endmodule

module ALU (
  input  [15:0] Source1,
  input  [15:0] Source2,
  input  ZFLD,
  input  CLOCK,
  input  [5:0] ALUControl,
  output [15:0] Output,
  output ZF
);

  wire or_2_out, register_1_q;
  wire [15:0] adder_1_out, adder_2_out, and_1_out, multiplexer_1_out, not_1_out, or_1_out, subtractor_1_out,
       subtractor_2_out, xor_1_out;

  Adder #(.width(16)) adder_1 (.a(Source2), .b(16'h1), .out(adder_1_out));  // open: cin, cout
  Subtractor #(.width(16)) subtractor_1 (.a(Source2), .b(16'h1), .out(subtractor_1_out));  // open: bin, bout
  assign not_1_out = ~Source1;  // NOT_Gate not_1, 16 bits wide
  Adder #(.width(16)) adder_2 (.a(Source1), .b(Source2), .out(adder_2_out));  // open: cin, cout
  Subtractor #(.width(16)) subtractor_2 (.a(Source1), .b(Source2), .out(subtractor_2_out));  // open: bin, bout
  assign and_1_out = Source1 & Source2;  // AND_Gate and_1, 16 bits wide
  assign or_1_out = Source1 | Source2;  // OR_Gate or_1, 16 bits wide
  assign xor_1_out = Source1 ^ Source2;  // XOR_Gate xor_1, 16 bits wide
  Multiplexer #(.select(3), .width(16), .enable("false")) multiplexer_1 (
    .in0(Source1), .in1(not_1_out), .in2(adder_1_out), .in3(subtractor_1_out), .out(multiplexer_1_out),
    .sel(ALUControl[2:0]));  // open: in4, in5, in6, in7
  Multiplexer #(.select(3), .width(16), .enable("false")) multiplexer_2 (
    .in0(adder_2_out), .in1(subtractor_2_out), .in2(and_1_out), .in3(or_1_out), .in4(xor_1_out),
    .in7(multiplexer_1_out), .out(Output), .sel(ALUControl[5:3]));  // open: in5, in6
  or or_2 (or_2_out, Output[0], Output[1], Output[2], Output[3], Output[4], Output[5], Output[6], Output[7], Output[8], Output[9], Output[10], Output[11], Output[12], Output[13], Output[14], Output[15]);
  Register #(.width(1)) register_1 (.D(or_2_out), .en(ZFLD), .Q(register_1_q), .clk(CLOCK));  // open: clr
  not not_2 (ZF, register_1_q);
endmodule

// PC
module PogramCOUNTER (
  input  [11:0] jumpin,
  input  Clk,
  input  PCLD,
  input  PCINC,
  input  [11:0] _1,
  output [11:0] \output 
);

  wire or_1_out;
  wire [11:0] adder_1_out, multiplexer_1_out;

  Multiplexer #(.width(12), .enable("false")) multiplexer_1 (
    .in0(adder_1_out), .in1(jumpin), .out(multiplexer_1_out), .sel(PCLD));
  Register #(.width(12)) register_1 (.D(multiplexer_1_out), .en(or_1_out), .Q(\output ), .clk(Clk));  // open: clr
  or or_1 (or_1_out, PCINC, PCLD);
  Adder #(.width(12)) adder_1 (.a(\output ), .b(_1), .out(adder_1_out));  // open: cin, cout
endmodule

// CPU
module yeni (
  input  [15:0] Dout,
  input  clock,
  output [11:0] ADDR,
  output MEMLD,
  output [15:0] Din
);

  wire alu_1_zf, controlunit_1_armux, controlunit_1_irld, controlunit_1_mux, controlunit_1_pcinc,
       controlunit_1_pcld, controlunit_1_regld, controlunit_1_zfld;
  wire [2:0] instructionsplitter_1_dest, instructionsplitter_1_src1, instructionsplitter_1_src2;
  wire [5:0] instructionsplitter_1_alucode;
  wire [11:0] adder_1_out, instructionsplitter_1_relative_offset, multiplexer_4_out, pogramcounter_1_output;
  wire [15:0] alu_1_output, multiplexer_2_out, registerfile_1_data_out1, registerfile_1_data_out2,
       registerfile_1_data_out3, registerfile_1_data_out4, registerfile_1_data_out5,
       registerfile_1_data_out6, registerfile_1_data_out7, registerfile_1_data_out8;
  wire [15:12] multiplexer_4_out_2;

  PogramCOUNTER pogramcounter_1 (
    .jumpin(adder_1_out), .PCLD(controlunit_1_pcld), .PCINC(controlunit_1_pcinc), ._1(12'h1),
    .\output (pogramcounter_1_output), .Clk(clock));
  Multiplexer #(.width(12), .enable("false")) multiplexer_1 (
    .in0(pogramcounter_1_output), .in1(multiplexer_4_out), .out(ADDR), .sel(controlunit_1_armux));
  Adder #(.width(12)) adder_1 (
    .a(instructionsplitter_1_relative_offset), .b(pogramcounter_1_output), .out(adder_1_out));  // open: cin, cout
  RegisterFile registerfile_1 (
    .rd(instructionsplitter_1_dest), .Datain(multiplexer_2_out), .Register_Load(controlunit_1_regld),
    .clock(clock), .Data_Out1(registerfile_1_data_out1), .Data_Out2(registerfile_1_data_out2),
    .Data_Out3(registerfile_1_data_out3), .Data_Out4(registerfile_1_data_out4),
    .Data_Out5(registerfile_1_data_out5), .Data_Out6(registerfile_1_data_out6),
    .Data_Out7(registerfile_1_data_out7), .Data_Out8(registerfile_1_data_out8));
  Multiplexer #(.width(16), .enable("false")) multiplexer_2 (
    .in0(alu_1_output), .in1(Dout), .out(multiplexer_2_out), .sel(controlunit_1_mux));
  Multiplexer #(.select(3), .width(16), .enable("false")) multiplexer_3 (
    .in0(registerfile_1_data_out1), .in1(registerfile_1_data_out2), .in2(registerfile_1_data_out3),
    .in3(registerfile_1_data_out4), .in4(registerfile_1_data_out5), .in5(registerfile_1_data_out6),
    .in6(registerfile_1_data_out7), .in7(registerfile_1_data_out8), .out(Din),
    .sel(instructionsplitter_1_src1));
  ALU alu_1 (
    .Source1(Din), .Source2({multiplexer_4_out_2, multiplexer_4_out}),
    .ALUControl(instructionsplitter_1_alucode), .Output(alu_1_output), .CLOCK(clock), .ZF(alu_1_zf),
    .ZFLD(controlunit_1_zfld));
  InstructionSplitter instructionsplitter_1 (
    .Instruction(Dout[11:0]), .IRLoad(controlunit_1_irld), .clk(clock),
    .ALUCode(instructionsplitter_1_alucode), .src1(instructionsplitter_1_src1),
    .src2(instructionsplitter_1_src2), .dest(instructionsplitter_1_dest),
    .relative_Offset(instructionsplitter_1_relative_offset));
  Multiplexer #(.select(3), .width(16), .enable("false")) multiplexer_4 (
    .in0(registerfile_1_data_out1), .in1(registerfile_1_data_out2), .in2(registerfile_1_data_out3),
    .in3(registerfile_1_data_out4), .in4(registerfile_1_data_out5), .in5(registerfile_1_data_out6),
    .in6(registerfile_1_data_out7), .in7(registerfile_1_data_out8),
    .out({multiplexer_4_out_2, multiplexer_4_out}), .sel(instructionsplitter_1_src2));
  ControlUnit controlunit_1 (
    .opcode(Dout[14:12]), .ZF(alu_1_zf), .CLOCK(clock), .Armux(controlunit_1_armux),
    .PCLD(controlunit_1_pcld), .REGLD(controlunit_1_regld), .IRLD(controlunit_1_irld),
    .PCINC(controlunit_1_pcinc), .mux(controlunit_1_mux), .MEMLD(MEMLD), .ZFLD(controlunit_1_zfld));

  // Notes on the sheet:
  //   Go to Control Unit
  //   Mux
  //   RegisterLoad
  //   IRLoad
  //   Armux
endmodule

module ControlUnit (
  input  [2:0] opcode,
  input  ZF,
  input  CLOCK,
  output IRLD,
  output PCINC,
  output mux,
  output Armux,
  output PCLD,
  output MEMLD,
  output REGLD,
  output ZFLD
);

  wire decoder_1_out1, not_1_out, not_2_out;
  wire [1:1] and_1_out;
  wire [2:0] multiplexer_1_out, multiplexer_2_out, register_1_q;

  and and_1 (and_1_out[1], opcode[2], not_1_out, not_2_out);
  not not_1 (not_1_out, opcode[1]);
  not not_2 (not_2_out, opcode[0]);
  Multiplexer #(.select(2), .width(3), .enable("false")) multiplexer_1 (
    .in0(opcode), .in1(opcode), .in2(3'b000), .in3(3'b101), .out(multiplexer_1_out), .sel({and_1_out[1], ZF}));
  Multiplexer #(.width(3), .enable("false")) multiplexer_2 (
    .in0(3'b000), .in1(multiplexer_1_out), .out(multiplexer_2_out), .sel(IRLD));
  Register #(.width(3)) register_1 (.D(multiplexer_2_out), .en(1'b1), .Q(register_1_q), .clk(CLOCK));  // open: clr
  Decoder #(.select(3), .enable("false")) decoder_1 (
    .out0(IRLD), .out1(decoder_1_out1), .out2(mux), .out3(MEMLD), .out5(PCLD), .out7(ZFLD), .sel(register_1_q));  // open: out4, out6
  or or_1 (REGLD, ZFLD, decoder_1_out1, mux);
  or or_2 (PCINC, IRLD, decoder_1_out1);
  or or_3 (Armux, MEMLD, mux);

  // Notes on the sheet:
  //   fetch
endmodule

module main (
);

  wire clock_1_out, yeni_1_memld;
  wire [11:0] yeni_1_addr;
  wire [15:0] ram_1_data, yeni_1_din;

  RAM #(.addrWidth(12), .dataWidth(16), .bus("separate")) ram_1 (
    .addr(yeni_1_addr), .din(yeni_1_din), .data(ram_1_data), .str(yeni_1_memld), .clk(clock_1_out), .ld(1'b1));  // open: sel, clr
  yeni yeni_1 (.ADDR(yeni_1_addr), .Dout(ram_1_data), .clock(clock_1_out), .Din(yeni_1_din), .MEMLD(yeni_1_memld));
  Clock clock_1 (.out(clock_1_out));
endmodule

module InstructionSplitter (
  input  [11:0] Instruction,
  input  IRLoad,
  input  clk,
  output [5:0] ALUCode,
  output [2:0] src1,
  output [2:0] src2,
  output [2:0] dest,
  output [11:0] relative_Offset
);

  Register #(.width(12)) register_1 (
    .D(Instruction), .en(IRLoad), .Q({ALUCode, relative_Offset[5:3], dest}), .clk(clk));  // open: clr

  assign {relative_Offset[11:6], relative_Offset[2:0]} = {ALUCode, dest};
  assign src1 = ALUCode[2:0];
  assign src2 = relative_Offset[5:3];
endmodule
